# Fritzing sketch Fluorestat_moterboard (saved by Fritzing 0.9.4)
circuit board: 14cm x 11.5cm
breadboards: 1

parts:
  Op_Amp = IC, DIP package, 8 pins [chip_label=IC]
  Op_Amp_2 = IC, DIP package, 8 pins [chip_label=IC]
  Converter = IC, DIP package, 8 pins [chip_label=IC]
  4_7K2 = Resistor [tolerance=±5% resistance=4.7k package=THT]
  4_7K3 = Resistor [tolerance=±5% resistance=4.7k package=THT]
  4_7K4 = Resistor [tolerance=±5% resistance=4.7k package=THT]
  C2 = Electrolytic Capacitor [capacitance=100µF package="100 mil [THT, electrolytic]"]
  J384 = female pin header, 1 pin [form="♀ (female)"]
  J385 = female pin header, 1 pin [form="♀ (female)"]
  Vial_1 = female pin header, 1 pin [form="♀ (female)"]
  J386 = female pin header, 1 pin [form="♀ (female)"]
  J387 = female pin header, 2 pins [form="♀ (female)"]
  J388 = female pin header, 6 pins [form="♀ (female)"]
  J389 = female pin header, 1 pin [form="♀ (female)"]
  J390 = female pin header, 1 pin [form="♀ (female)"]
  J391 = female pin header, 1 pin [form="♀ (female)"]
  J392 = female pin header, 1 pin [form="♀ (female)"]
  J393 = female pin header, 1 pin [form="♀ (female)"]
  J394 = female pin header, 1 pin [form="♀ (female)"]
  J395 = female pin header, 1 pin [form="♀ (female)"]
  J396 = female pin header, 1 pin [form="♀ (female)"]
  J397 = female pin header, 1 pin [form="♀ (female)"]
  J398 = female pin header, 1 pin [form="♀ (female)"]
  J399 = female pin header, 1 pin [form="♀ (female)"]
  Arduino_Mega1 = Arduino Mega 2560 (Rev3)
  390 = Resistor [tolerance=±5% resistance=390 package=THT]
  1M = Resistor [tolerance=±5% resistance=390 package=THT]
  390_2 = Resistor [tolerance=±5% resistance=390 package=THT]
  390_3 = Resistor [tolerance=±5% resistance=390 package=THT]
  390_4 = Resistor [tolerance=±5% resistance=390 package=THT]
  D68 = Diode [package=diode-1n4148]
  GND = female pin header, 1 pin [form="♀ (female)"]
  5V = female pin header, 1 pin [form="♀ (female)"]
  -_Diode_+5 = Diode [package=diode-1n4148]
  12V = female pin header, 1 pin [form="♀ (female)"]
  NPN = NPN-Transistor [package="TO92 [THT]"]
  P-ch = NPN-Transistor [package="TO92 [THT]"]
  NPN_2 = NPN-Transistor [package="TO92 [THT]"]
  NPN_3 = NPN-Transistor [package="TO92 [THT]"]
  Sensor_1 = screw terminal, 6 pins
  Driver_1 = screw terminal, 2 pins
  10u8 = Ceramic Capacitor [capacitance=10µF package="200 mil [THT, multilayer]"]
  10u = Ceramic Capacitor [capacitance=10µF package="200 mil [THT, multilayer]"]
  10u7 = Ceramic Capacitor [capacitance=10µF package="200 mil [THT, multilayer]"]
  10u6 = Ceramic Capacitor [capacitance=10µF package="200 mil [THT, multilayer]"]
  10u5 = Ceramic Capacitor [capacitance=10µF package="200 mil [THT, multilayer]"]
  Op_Amp_3 = IC, DIP package, 8 pins [chip_label=IC]
  10u12 = Ceramic Capacitor [capacitance=10µF package="200 mil [THT, multilayer]"]
  10u13 = Ceramic Capacitor [capacitance=10µF package="200 mil [THT, multilayer]"]
  4_7K5 = Resistor [tolerance=±5% resistance=4.7k package=THT]
  47K = Resistor [tolerance=±5% resistance=47k package=THT]
  4_7K7 = Resistor [tolerance=±5% resistance=4.7k package=THT]
  C3 = Electrolytic Capacitor [capacitance=100µF package="100 mil [THT, electrolytic]"]
  Sensor_2 = screw terminal, 6 pins
  Detector = screw terminal, 2 pins
  Driver_2 = screw terminal, 2 pins
  R2 = Resistor [tolerance=±5% resistance=4.7k package=THT]
  390_5 = Resistor [tolerance=±5% resistance=390 package=THT]
  100 = Resistor [tolerance=±5% resistance=390 package=THT]
  Fans = screw terminal, 4 pins
  NPN_4 = NPN-Transistor [package="TO92 [THT]"]
  NPN_5 = NPN-Transistor [package="TO92 [THT]"]

nets:
  N1: Op_Amp.pin1, Op_Amp.pin2, 4_7K4.Pin_0
  N2: Op_Amp.pin3, 4_7K3.Pin_1, 10u8.1
  N3: Op_Amp.pin4, Op_Amp_2.pin4, Converter.pin3, C2.+, J388.pin4, J396.pin1, Arduino_Mega1.GND, GND.pin1, NPN.E, NPN_2.E, NPN_3.E, Sensor_1.pin5, Sensor_1.pin6, Driver_1.pin2, 10u8.0, 10u.0, 10u6.1, 10u5.1, Op_Amp_3.pin4, 10u12.1, 10u13.0, 47K.Pin_1, C3.+, Sensor_2.pin5, Sensor_2.pin6, Detector.pin2, Driver_2.pin2, Fans.pin2, Fans.pin4, NPN_4.E, NPN_5.E
  N4: Op_Amp.pin5, 4_7K4.Pin_1, Arduino_Mega1.A0, 10u.1
  N5: Op_Amp.pin6, Op_Amp.pin7, Driver_1.pin1
  N6: Op_Amp.pin8, Op_Amp_2.pin8, Converter.pin8, Arduino_Mega1.5V, Sensor_1.pin1, 10u5.0, Op_Amp_3.pin8, Sensor_2.pin1
  N7: Op_Amp_2.pin1, Op_Amp_2.pin2, Arduino_Mega1.A5, Sensor_2.pin2
  N8: Op_Amp_2.pin3, C3.-, R2.Pin_1
  N9: Op_Amp_2.pin5, 4_7K2.Pin_1, C2.-
  N10: Op_Amp_2.pin6, Op_Amp_2.pin7, Arduino_Mega1.A2, Sensor_1.pin2
  N11: Converter.pin2, 10u7.0
  N12: Converter.pin4, 10u7.1
  N13: Converter.pin5, Sensor_1.pin3, 10u6.0, Sensor_2.pin3
  N14: 4_7K2.Pin_0, Arduino_Mega1.D11_PWM
  N15: 4_7K3.Pin_0, Arduino_Mega1.D12_PWM
  N16: J384.pin1, J387.pin2
  N17: J385.pin1, NPN_5.C
  N18: Vial_1.pin1, J387.pin1
  N19: J386.pin1, P-ch.C
  N20: J388.pin1, Arduino_Mega1.D5_PWM
  N21: J388.pin2, Arduino_Mega1.D4_PWM
  N22: J388.pin3, Arduino_Mega1.D3_PWM
  N23: J388.pin6, 1M.Pin_0, 5V.pin1, P-ch.E
  N24: J389.pin1, Arduino_Mega1.A13
  N25: J390.pin1, Arduino_Mega1.A12
  N26: J391.pin1, Arduino_Mega1.A15
  N27: J392.pin1, D68.A, NPN_3.C
  N28: J393.pin1, Arduino_Mega1.A14
  N29: J394.pin1, NPN_4.C
  N30: J395.pin1, -_Diode_+5.A, NPN_2.C
  N31: J397.pin1, J398.pin1, D68.C, -_Diode_+5.C, 12V.pin1, Fans.pin1, Fans.pin3
  N32: J399.pin1, NPN.C
  N33: Arduino_Mega1.A9, Sensor_2.pin4
  N34: Arduino_Mega1.A3, Sensor_1.pin4
  N35: Arduino_Mega1.A6, 47K.Pin_0, Detector.pin1
  N36: Arduino_Mega1.A7, Op_Amp_3.pin5, 10u12.0, 4_7K5.Pin_1
  N37: Arduino_Mega1.D21/SCL, Arduino_Mega1.SCL, 390_2.Pin_1
  N38: Arduino_Mega1.D19/RX1, 390.Pin_1
  N39: Arduino_Mega1.D17_PWM/RX2, 390_5.Pin_1
  N40: Arduino_Mega1.D14/TX3, 1M.Pin_1, 100.Pin_1
  N41: Arduino_Mega1.D9_PWM, R2.Pin_0
  N42: Arduino_Mega1.D8_PWM, 4_7K7.Pin_0
  N43: Arduino_Mega1.D2_PWM, 390_3.Pin_0
  N44: Arduino_Mega1.D26, 390_4.Pin_0
  N45: 390.Pin_0, NPN_4.B
  N46: 390_2.Pin_0, NPN.B
  N47: 390_3.Pin_1, NPN_3.B
  N48: 390_4.Pin_1, NPN_2.B
  N49: P-ch.B, 100.Pin_0
  N50: Op_Amp_3.pin1, Op_Amp_3.pin2, 4_7K5.Pin_0
  N51: Op_Amp_3.pin3, 10u13.1, 4_7K7.Pin_1
  N52: Op_Amp_3.pin6, Op_Amp_3.pin7, Driver_2.pin1
  N53: 390_5.Pin_0, NPN_5.B

notes:
  GND
  Blk
  Thk
  R
  G
  W
  B
  Thick
  Black
  Thick GND
  Voltage
  Red
  12V
  Two Colour
