# Fritzing sketch Hub (saved by Fritzing 0.9.3b)
circuit board: 6.4cm x 12cm
breadboards: 1

parts:
  1_5K = Resistor [tolerance=±5% resistance=220 package=THT]
  750 = Resistor [tolerance=±5% resistance=390 package=THT]
  82 = Resistor [tolerance=±5% resistance=75 package=THT]
  J10 = female pin header, 1 pin [form="♀ (female)"]
  J11 = female pin header, 1 pin [form="♀ (female)"]
  J12 = female pin header, 1 pin [form="♀ (female)"]
  J13 = female pin header, 1 pin [form="♀ (female)"]
  J23 = female pin header, 1 pin [form="♀ (female)"]
  J24 = female pin header, 1 pin [form="♀ (female)"]
  J25 = female pin header, 1 pin [form="♀ (female)"]
  J26 = female pin header, 1 pin [form="♀ (female)"]
  J27 = female pin header, 1 pin [form="♀ (female)"]
  J28 = female pin header, 1 pin [form="♀ (female)"]
  J29 = female pin header, 1 pin [form="♀ (female)"]
  J30 = female pin header, 1 pin [form="♀ (female)"]
  J31 = female pin header, 1 pin [form="♀ (female)"]
  J32 = female pin header, 1 pin [form="♀ (female)"]
  J33 = female pin header, 1 pin [form="♀ (female)"]
  750_2 = Resistor [tolerance=±5% resistance=75 package=THT]
  Fan = LEDs [package=led-1206]
  LED = LEDs [package=led-1206]
  Heater = LEDs [package=led-1206]
  J37 = female pin header, 1 pin [form="♀ (female)"]
  J38 = female pin header, 1 pin [form="♀ (female)"]
  J39 = female pin header, 1 pin [form="♀ (female)"]
  82_2 = Resistor [tolerance=±5% resistance=100 package=THT]
  J4 = screw terminal, 12 pins
  J5 = screw terminal, 12 pins
  OD_Regulator = Voltage Regulator [package=to220-igo]
  Sensor_Regulator = Voltage Regulator [package=to220-igo]
  Level_Regulator = Voltage Regulator [package=to220-igo]

nets:
  N1: 1_5K.Pin_0, Heater.C
  GND: 1_5K.Pin_1, J13.pin1, J39.pin1, J4.pin9, J4.pin12, J5.pin5, J5.pin9, J5.pin12, OD_Regulator.GND, Sensor_Regulator.GND, Level_Regulator.GND
  N2: 750.Pin_0, LED.A
  N3: 750.Pin_1, 82.Pin_0, OD_Regulator.OUT
  N4: 82.Pin_1, J4.pin5
  N5: J10.pin1, Fan.C, J5.pin1
  N6: J11.pin1, 750_2.Pin_1, J4.pin4, J5.pin2, J5.pin3, Sensor_Regulator.IN
  N7: J12.pin1, OD_Regulator.IN, Level_Regulator.IN
  N8: J23.pin1, J4.pin3
  N9: J24.pin1, LED.C, J4.pin6
  N10: J25.pin1, J4.pin11
  N11: J26.pin1, J5.pin4
  N12: J27.pin1, J5.pin8
  N13: J28.pin1, J4.pin8
  N14: J29.pin1, J5.pin11
  N15: J30.pin1, Heater.A, J5.pin6
  N16: J31.pin1, J37.pin1
  N17: J32.pin1, J4.pin2
  N18: J33.pin1, J38.pin1
  N19: 750_2.Pin_0, Fan.A
  N20: 82_2.Pin_0, Level_Regulator.OUT
  N21: 82_2.Pin_1, J4.pin1
  N22: J4.pin7, J4.pin10, J5.pin7, J5.pin10, Sensor_Regulator.OUT

notes:
  5V
  OD data
  GND
  level LED 5V
  level LED GND
  pump GND
  pump 12V
  OD LED 5V
  OD LED GND
  level LED data
  level data
  OD LED data
  heat 5V (Blk)
  fan GND
  heat GND (Red)
  fan 12V
  _____________
