# Fritzing sketch SSR (saved by Fritzing 0.9.4)
circuit board: 1.45626cm x 2.99057cm
breadboards: 1

parts:
  SSR = IC, DIP package, 6 pins [chip_label=IC]
  part = female pin header, 2 pins [form="♀ (female)"]

nets:
  N1: SSR.pin1, part.pin1
  N2: SSR.pin2, part.pin2

notes:
  AC Load
  +LED
  -LED
